# Fritzing sketch Wifi_Radio_Wiring (saved by Fritzing 0.9.3b)
breadboards: 1

parts:
  Raspberry_Pi1 = Raspberry Pi B rev2
  Bauteil1 = Arduino Pro Mini v13
  Bauteil2 = Arduino Pro Mini v13
  U1 = LCD-16X2 [package=lcd-16x2]
  Bauteil3 = Logic Level Converter
  ENC_KURZ = Rotary Encoder with Knob
  ENC_LANG = Rotary Encoder with Knob
  S1 = Pushbutton [package="[THT]"]
  S2 = Pushbutton [package="[THT]"]
  S3 = Pushbutton [package="[THT]"]
  S4 = Pushbutton [package="[THT]"]
  R2 = Resistor [tolerance=±5% resistance=10k package=THT]
  R3 = Resistor [tolerance=±5% resistance=10k package=THT]
  R4 = Resistor [tolerance=±5% resistance=10k package=THT]
  R5 = Resistor [tolerance=±5% resistance=10k package=THT]
  Power_plug1 = Power plug
  R1 = Resistor [tolerance=±5% resistance=680 package=THT]

nets:
  N1: Raspberry_Pi1.3V3, Bauteil3.LV
  N2: Raspberry_Pi1.GPIO_3, ENC_LANG.no_name_yet#4
  GND: Raspberry_Pi1.GND, Bauteil1.GND, Bauteil1.RESET, Bauteil2.GND, U1.VSS, U1.VO, U1.R_W, U1.K, Bauteil3.GND, ENC_KURZ.no_name_yet#2, ENC_KURZ.no_name_yet#5, ENC_LANG.no_name_yet#2, ENC_LANG.no_name_yet#5, R2.Pin_1, R3.Pin_1, R4.Pin_1, R5.Pin_1
  N3: Raspberry_Pi1.GPIO_23, U1.DB6
  N4: Raspberry_Pi1.GPIO_14, Bauteil3.TX2_LV
  N5: Raspberry_Pi1.GPIO_15, Bauteil3.RX2_LV
  N6: Raspberry_Pi1.GPIO_18, U1.DB7
  N7: Raspberry_Pi1.GPIO_27, Bauteil3.RX_LV
  N8: Raspberry_Pi1.GPIO_22, Bauteil3.TX_LV
  N9: Raspberry_Pi1.GPIO_24, U1.DB5
  N10: Raspberry_Pi1.GPIO_25, U1.DB4
  N11: Raspberry_Pi1.GPIO_8, U1.E
  N12: Raspberry_Pi1.GPIO_7, U1.RS
  VCC: Bauteil1.VCC, Bauteil2.VCC, U1.VDD, Bauteil3.HV, S1.Pin_3, S1.Pin_4, S2.Pin_3, S2.Pin_4, S3.Pin_3, S3.Pin_4, S4.Pin_3, S4.Pin_4, Power_plug1.VCC, R1.Pin_0
  N13: Bauteil1.A3, ENC_KURZ.no_name_yet#1
  N14: Bauteil1.A2, ENC_KURZ.no_name_yet#3
  N15: Bauteil1.A1, ENC_KURZ.no_name_yet#4
  N16: Bauteil1.A0, S1.Pin_2
  N17: Bauteil1.D13/SCK, S2.Pin_2
  N18: Bauteil1.D12/MISO, S3.Pin_2
  N19: Bauteil1.D11_PWM/MOSI, S4.Pin_2
  N20: Bauteil1.D1/RX, Bauteil3.TX2_HV
  N21: Bauteil1.D0/TX, Bauteil3.RX2_HV
  N22: Bauteil2.A3, ENC_LANG.no_name_yet#3
  N23: Bauteil2.A2, ENC_LANG.no_name_yet#1
  N24: Bauteil2.A1, Bauteil3.RX_HV
  N25: Bauteil2.A0, Bauteil3.TX_HV
  N26: U1.A, R1.Pin_1

custom parts:
  Rotary Encoder with Knob: Rotary Encoder with 1/4" Shaft and Knob
